// Logisim project Single_Cycle_Procesessor.circ as structural Verilog: 11 circuits, main circuit Single_Cycle_Processor
// Regiser_File
module Register_File (
  input  [2:0] RA,
  input  [2:0] RB,
  input  [2:0] RW,
  input  [15:0] BusW,
  input  Reg_Write,
  input  clk,
  output [15:0] BusA,
  output [15:0] BusB
);

  wire A_D0, A_D1, A_D2, A_D3, A_D4, A_D5, A_D6, A_D7, and_1_out, and_2_out, and_3_out, and_4_out, and_5_out,
       and_6_out, and_7_out, B_D0, B_D1, B_D2, B_D3, B_D4, B_D5, B_D6, B_D7, R1_Enable, R2_Enable, R3_Enable,
       R4_Enable, R5_Enable, R6_Enable, R7_Enable;
  wire [15:0] R1_2_q, R1_q, R2_q, R3_q, R4_q, R5_q, R6_q, R7_q;

  Decoder #(.select(3), .enable("false")) decoder_1 (
    .out0(A_D0), .out1(A_D1), .out2(A_D2), .out3(A_D3), .out4(A_D4), .out5(A_D5), .out6(A_D6), .out7(A_D7),
    .sel(RA));
  Decoder #(.select(3), .enable("false")) decoder_2 (
    .out0(B_D0), .out1(B_D1), .out2(B_D2), .out3(B_D3), .out4(B_D4), .out5(B_D5), .out6(B_D6), .out7(B_D7),
    .sel(RB));
  Decoder #(.select(3), .enable("false")) decoder_3 (
    .out1(R1_Enable), .out2(R2_Enable), .out3(R3_Enable), .out4(R4_Enable), .out5(R5_Enable),
    .out6(R6_Enable), .out7(R7_Enable), .sel(RW));  // open: out0
  and and_1 (and_1_out, Reg_Write, R1_Enable);
  and and_2 (and_2_out, Reg_Write, R2_Enable);
  and and_3 (and_3_out, Reg_Write, R3_Enable);
  and and_4 (and_4_out, Reg_Write, R4_Enable);
  and and_5 (and_5_out, Reg_Write, R5_Enable);
  and and_6 (and_6_out, Reg_Write, R6_Enable);
  and and_7 (and_7_out, Reg_Write, R7_Enable);
  Register #(.width(16)) R1 (.D({16{1'b0}}), .Q(R1_q), .clk(clk));  // open: en, clr
  Register #(.width(16)) R1_2 (.D(BusW), .en(and_1_out), .Q(R1_2_q), .clk(clk));  // open: clr
  Register #(.width(16)) R2 (.D(BusW), .en(and_2_out), .Q(R2_q), .clk(clk));  // open: clr
  Register #(.width(16)) R3 (.D(BusW), .en(and_3_out), .Q(R3_q), .clk(clk));  // open: clr
  Register #(.width(16)) R4 (.D(BusW), .en(and_4_out), .Q(R4_q), .clk(clk));  // open: clr
  Register #(.width(16)) R5 (.D(BusW), .en(and_5_out), .Q(R5_q), .clk(clk));  // open: clr
  Register #(.width(16)) R6 (.D(BusW), .en(and_6_out), .Q(R6_q), .clk(clk));  // open: clr
  Register #(.width(16)) R7 (.D(BusW), .en(and_7_out), .Q(R7_q), .clk(clk));  // open: clr
  assign BusB = B_D0 ? R1_q : 16'bz;  // Controlled_Buffer controlled_buffer_1
  assign BusB = B_D1 ? R1_2_q : 16'bz;  // Controlled_Buffer controlled_buffer_2
  assign BusB = B_D2 ? R2_q : 16'bz;  // Controlled_Buffer controlled_buffer_3
  assign BusB = B_D3 ? R3_q : 16'bz;  // Controlled_Buffer controlled_buffer_4
  assign BusB = B_D4 ? R4_q : 16'bz;  // Controlled_Buffer controlled_buffer_5
  assign BusB = B_D5 ? R5_q : 16'bz;  // Controlled_Buffer controlled_buffer_6
  assign BusB = B_D6 ? R6_q : 16'bz;  // Controlled_Buffer controlled_buffer_7
  assign BusB = B_D7 ? R7_q : 16'bz;  // Controlled_Buffer controlled_buffer_8
  assign BusA = A_D0 ? R1_q : 16'bz;  // Controlled_Buffer controlled_buffer_9
  assign BusA = A_D1 ? R1_2_q : 16'bz;  // Controlled_Buffer controlled_buffer_10
  assign BusA = A_D2 ? R2_q : 16'bz;  // Controlled_Buffer controlled_buffer_11
  assign BusA = A_D3 ? R3_q : 16'bz;  // Controlled_Buffer controlled_buffer_12
  assign BusA = A_D4 ? R4_q : 16'bz;  // Controlled_Buffer controlled_buffer_13
  assign BusA = A_D5 ? R5_q : 16'bz;  // Controlled_Buffer controlled_buffer_14
  assign BusA = A_D6 ? R6_q : 16'bz;  // Controlled_Buffer controlled_buffer_15
  assign BusA = A_D7 ? R7_q : 16'bz;  // Controlled_Buffer controlled_buffer_16
endmodule

module ALU (
  input  [15:0] A,
  input  [15:0] B,
  input  [2:0] ALU_Function,
  input  Opcode0_1_Select,
  input  [15:0] INC_PC,
  output ZERO,
  output [15:0] ALU_Output,
  output [11:0] Immediate_JR_JALR
);

  wire [15:0] au_1_arithmetic_output, lu_and_shifter_1_opcode0_output, nor_1_out;

  LU_and_Shifter lu_and_shifter_1 (
    .Opcode0_Output(lu_and_shifter_1_opcode0_output), .A(A), .B(B), .Opcode0_Select(ALU_Function));
  AU au_1 (.Arithmetic_Output(au_1_arithmetic_output), .A(A), .B(B), .Arithmetic_Select(ALU_Function), .INC_PC(INC_PC));
  Multiplexer #(.width(16), .enable("false")) multiplexer_1 (
    .in0(lu_and_shifter_1_opcode0_output), .in1(au_1_arithmetic_output), .out(ALU_Output),
    .sel(Opcode0_1_Select));
  assign {{8{nor_1_out[15]}}, nor_1_out[7:0]} = ~(ALU_Output | ALU_Output);  // NOR_Gate nor_1, 16 bits wide
  and and_1 (ZERO, nor_1_out[0], nor_1_out[1], nor_1_out[2], nor_1_out[3], nor_1_out[4], nor_1_out[5], nor_1_out[6], nor_1_out[7], nor_1_out[15], nor_1_out[15], nor_1_out[15], nor_1_out[15], nor_1_out[15], nor_1_out[15], nor_1_out[15], nor_1_out[15]);

  assign Immediate_JR_JALR = A[11:0];

  // Other names for the same wires on the sheet: opcode_Select = Opcode0_1_Select
endmodule

module Logical_Unit (
  input  [15:0] A,
  input  [15:0] B,
  output [15:0] AND_Output,
  output [15:0] OR_Output,
  output [15:0] NOR_Output,
  output [15:0] XOR_Output
);

  assign AND_Output = B & A;  // AND_Gate AND, 16 bits wide
  assign OR_Output = B | A;  // OR_Gate OR, 16 bits wide
  assign XOR_Output = B ^ A;  // XOR_Gate XOR, 16 bits wide
  assign NOR_Output = ~OR_Output;  // NOT_Gate not_1, 16 bits wide
endmodule

module Shifter (
  input  [3:0] Shift_Amount,
  input  [15:0] Number,
  output [15:0] SLL_Output,
  output [15:0] SRL_Output,
  output [15:0] SRA_Output,
  output [15:0] ROL_Output
);

  Shifter_part #(.width(16)) shifter_1 (.in(Number), .\dist (Shift_Amount), .out(SLL_Output));
  Shifter_part #(.width(16), .shift("lr")) shifter_2 (.in(Number), .\dist (Shift_Amount), .out(SRL_Output));
  Shifter_part #(.width(16), .shift("ar")) shifter_3 (.in(Number), .\dist (Shift_Amount), .out(SRA_Output));
  Shifter_part #(.width(16), .shift("rl")) shifter_4 (.in(Number), .\dist (Shift_Amount), .out(ROL_Output));
endmodule

module AU (
  input  [15:0] A,
  input  [15:0] B,
  input  [2:0] Arithmetic_Select,
  input  [15:0] INC_PC,
  output [15:0] Arithmetic_Output
);

  wire subtractor_1_bout, subtractor_2_bout, xor_1_out;
  wire [15:0] Add_Output, Different_sign_Comp, nor_1_out, or_1_out, or_2_out, SLT, SLTE, SLTEU, SLTU,
       Sub_Output;

  xor xor_1 (xor_1_out, A[15], B[15]);
  Adder #(.width(16)) adder_1 (.a(A), .b(B), .out(Add_Output));  // open: cin, cout
  Subtractor #(.width(16)) subtractor_1 (.a(A), .b(B), .out(Sub_Output), .bout(subtractor_1_bout));  // open: bin
  Subtractor #(.width(1)) subtractor_2 (.a(B[15]), .b(A[15]), .bout(subtractor_2_bout));  // open: out, bin
  assign SLTU = {{15{1'b0}}, subtractor_1_bout};  // Bit_Extender bit_extender_1
  Multiplexer #(.width(16), .enable("false")) multiplexer_1 (
    .in0(SLTU), .in1(Different_sign_Comp), .out(SLT), .sel(xor_1_out));
  assign Different_sign_Comp = {{15{1'b0}}, subtractor_2_bout};  // Bit_Extender bit_extender_2
  assign nor_1_out = ~({16{1'b0}} | Sub_Output);  // NOR_Gate nor_1, 16 bits wide
  assign or_1_out = SLTU | nor_1_out;  // OR_Gate or_1, 16 bits wide
  assign or_2_out = nor_1_out | SLT;  // OR_Gate or_2, 16 bits wide
  assign SLTEU = {{15{1'b0}}, or_1_out[0]};  // Bit_Extender bit_extender_3
  assign SLTE = {{15{1'b0}}, or_2_out[0]};  // Bit_Extender bit_extender_4
  Multiplexer #(.select(3), .width(16), .enable("false")) multiplexer_2 (
    .in0(Add_Output), .in1(Sub_Output), .in2(SLT), .in3(SLTU), .in4(SLTE), .in5(SLTEU), .in7(INC_PC),
    .out(Arithmetic_Output), .sel(Arithmetic_Select));  // open: in6
endmodule

// LU&Shifter
module LU_and_Shifter (
  input  [15:0] A,
  input  [15:0] B,
  input  [2:0] Opcode0_Select,
  output [15:0] Opcode0_Output
);

  wire [15:0] logical_unit_1_and_output, logical_unit_1_nor_output, logical_unit_1_or_output,
       logical_unit_1_xor_output, shifter_1_rol_output, shifter_1_sll_output, shifter_1_sra_output,
       shifter_1_srl_output;

  Logical_Unit logical_unit_1 (
    .B(B), .A(A), .AND_Output(logical_unit_1_and_output), .OR_Output(logical_unit_1_or_output),
    .NOR_Output(logical_unit_1_nor_output), .XOR_Output(logical_unit_1_xor_output));
  Shifter shifter_1 (
    .Shift_Amount(B[3:0]), .Number(A), .SLL_Output(shifter_1_sll_output), .SRL_Output(shifter_1_srl_output),
    .SRA_Output(shifter_1_sra_output), .ROL_Output(shifter_1_rol_output));
  Multiplexer #(.select(3), .width(16), .enable("false")) multiplexer_1 (
    .in0(logical_unit_1_and_output), .in1(logical_unit_1_or_output), .in2(logical_unit_1_xor_output),
    .in3(logical_unit_1_nor_output), .in4(shifter_1_sll_output), .in5(shifter_1_srl_output),
    .in6(shifter_1_sra_output), .in7(shifter_1_rol_output), .out(Opcode0_Output), .sel(Opcode0_Select));
endmodule

module Single_Cycle_Processor (
  input  [15:0] r1,
  input  [15:0] r1_2,
  output pcsrc,
  output [15:0] alu,
  output [2:0] fun
);

  wire alu_1_zero, ALU_Src, BEQ, BGTZ, BLTZ, BNE, clock_1_out, Ext_opr, J, JAL, JALR, JR, LUI,
       main_controller_1_alu_control, MemRead, MemToReg, MemWrite, or_1_out, Reg_Dst, Reg_Write;
  wire [2:0] Funtion, multiplexer_2_out, multiplexer_3_out, multiplexer_5_out;
  wire [3:0] Opcode;
  wire [11:0] adder_1_out, alu_1_immediate_jr_jalr, multiplexer_1_out, multiplexer_7_out, Next_Instruction,
       pc_1_pc_output;
  wire [11:3] Immediate12;
  wire [15:0] bit_extender_2_out, bit_extender_3_out, BusB, BusWFromMem, INC_PC, multiplexer_4_out,
       multiplexer_6_out, multiplexer_8_out, ram_1_data, register_file_1_busa, shifter_1_out;

  Multiplexer #(.width(12), .enable("false")) multiplexer_1 (
    .in0(adder_1_out), .in1(Next_Instruction), .out(multiplexer_1_out), .sel(pcsrc));
  PC pc_1 (.PC_Input(multiplexer_1_out), .PC_Output(pc_1_pc_output));
  Adder #(.width(12)) adder_1 (.a(12'h1), .b(pc_1_pc_output), .out(adder_1_out));  // open: cin, cout
  assign INC_PC = {{4{1'b0}}, adder_1_out};  // Bit_Extender bit_extender_1
  ROM #(.addrWidth(12), .dataWidth(16)) rom_1 (
    .addr(pc_1_pc_output), .data({Opcode, Immediate12, Funtion}));  // open: sel
  assign bit_extender_2_out = {{4{1'b0}}, {Immediate12, Funtion}};  // Bit_Extender bit_extender_2
  Main_Controller main_controller_1 (
    .Instruction_Input({Opcode, Immediate12, Funtion}), .Reg_Dst(Reg_Dst), .Reg_Write(Reg_Write),
    .Ext_Op(Ext_opr), .ALU_Src(ALU_Src), .BEQ(BEQ), .BNE(BNE), .BGTZ(BGTZ), .BLTZ(BLTZ), .J(J),
    .Mem_Read(MemRead), .Mem_Write(MemWrite), .Mem_to_Reg(MemToReg), .Function_Code_Output(fun),
    .ALU_Control(main_controller_1_alu_control), .LUI(LUI), .JALR(JALR), .JR(JR), .JAL(JAL));
  Shifter_part #(.width(16)) shifter_1 (.in(bit_extender_2_out), .\dist (4'b0100), .out(shifter_1_out));
  Multiplexer #(.width(3), .enable("false")) multiplexer_2 (
    .in0(Immediate12[8:6]), .in1(Immediate12[5:3]), .out(multiplexer_2_out), .sel(Reg_Dst));
  Multiplexer #(.width(3), .enable("false")) multiplexer_3 (
    .in0(3'b001), .in1(3'b111), .out(multiplexer_3_out), .sel(JAL));
  Multiplexer #(.width(16), .enable("false")) multiplexer_4 (
    .in0(shifter_1_out), .in1(INC_PC), .out(multiplexer_4_out), .sel(JAL));
  Multiplexer #(.width(3), .enable("false")) multiplexer_5 (
    .in0(multiplexer_2_out), .in1(multiplexer_3_out), .out(multiplexer_5_out), .sel(or_1_out));
  or or_1 (or_1_out, JAL, LUI);
  Register_File register_file_1 (
    .RW(multiplexer_5_out), .RA(Immediate12[11:9]), .RB(Immediate12[8:6]), .Reg_Write(Reg_Write),
    .BusW(multiplexer_6_out), .BusA(register_file_1_busa), .BusB(BusB), .clk(clock_1_out));
  Clock clock_1 (.out(clock_1_out));
  Multiplexer #(.width(16), .enable("false")) multiplexer_6 (
    .in0(BusWFromMem), .in1(multiplexer_4_out), .out(multiplexer_6_out), .sel(or_1_out));
  Multiplexer #(.width(12), .enable("false")) multiplexer_7 (
    .in0({Immediate12, Funtion}), .in1(alu_1_immediate_jr_jalr), .out(multiplexer_7_out), .sel(JR));
  Multiplexer #(.width(16), .enable("false")) multiplexer_8 (
    .in0(BusB), .in1(bit_extender_3_out), .out(multiplexer_8_out), .sel(ALU_Src));
  assign bit_extender_3_out = {{10{1'b0}}, {Immediate12[5:3], Funtion}};  // Bit_Extender bit_extender_3
  ALU alu_1 (
    .ALU_Function(fun), .ALU_Output(alu), .A(register_file_1_busa), .B(multiplexer_8_out),
    .Opcode0_1_Select(main_controller_1_alu_control), .ZERO(alu_1_zero),
    .Immediate_JR_JALR(alu_1_immediate_jr_jalr), .INC_PC(INC_PC));
  NextPC1 nextpc1_1 (
    .INC_PC(adder_1_out), .Immediate(multiplexer_7_out), .Next_Instrucrion(Next_Instruction), .PCSrc(pcsrc),
    .J(J), .BLTZ(BLTZ), .Sign(register_file_1_busa[15]), .Zero(alu_1_zero), .BGTZ(BLTZ), .BEQ(BEQ), .BNE(BNE));
  RAM #(.addrWidth(16), .dataWidth(16), .bus("separate")) ram_1 (
    .addr(alu), .din(BusB), .data(ram_1_data), .str(MemWrite), .ld(MemRead));  // open: sel, clk, clr
  Multiplexer #(.width(16), .enable("false")) multiplexer_9 (
    .in0(alu), .in1(ram_1_data), .out(BusWFromMem), .sel(MemToReg));

  // Other names for the same wires on the sheet: Rt[2:0] = Immediate12[8:6]; Rs[2:0] = Immediate12[11:9];
  //   Immediate12[2:0] = Funtion; Rd[2:0] = Immediate12[5:3]

  // Notes on the sheet:
  //   contents of rom_1 (hex, n*v repeats v):
  //   b003 8482 86c3 8241 1e06
endmodule

module Main_Controller (
  input  [15:0] Instruction_Input,
  output [2:0] Function_Code_Output,
  output ALU_Control,
  output JALR,
  output JR,
  output Reg_Dst,
  output Reg_Write,
  output Ext_Op,
  output ALU_Src,
  output BEQ,
  output BNE,
  output BGTZ,
  output BLTZ,
  output Mem_Read,
  output Mem_Write,
  output Mem_to_Reg,
  output LUI,
  output J,
  output JAL
);

  wire ADDI, ANDI, BEQ_t, BGEZ, BGTZ_t, BLEZ, BLTZ_t, J_t, nor_1_out, nor_2_out, ORI, Rtype0000, Rtype0001;
  wire [2:0] bit_extender_1_out;

  Decoder #(.select(4), .enable("false")) decoder_1 (
    .out0(Rtype0000), .out1(Rtype0001), .out2(Mem_Read), .out3(Mem_Write), .out4(BEQ_t), .out5(BNE),
    .out6(ANDI), .out7(ORI), .out8(ADDI), .out9(J_t), .out10(LUI), .out11(JAL), .out12(BLTZ_t), .out13(BLEZ),
    .out14(BGTZ_t), .out15(BGEZ), .sel(Instruction_Input[15:12]));
  or or_1 (Reg_Dst, Rtype0000, Rtype0001);
  or or_2 (Reg_Write, Rtype0000, Rtype0001, Mem_Read, ANDI, ORI, ADDI, JAL, LUI);
  or or_3 (Ext_Op, Mem_Read, Mem_Write, ADDI);
  or or_4 (ALU_Src, Mem_Read, Mem_Write, ANDI, ORI, ADDI);
  or or_5 (BEQ, BEQ_t, BLEZ, BGEZ);
  or or_6 (BGTZ, BGEZ, BGTZ_t);
  or or_7 (BLTZ, BLEZ, BLTZ_t);
  or or_8 (J, J_t, JAL, JR);
  nor nor_1 (nor_1_out, Rtype0000, Rtype0001);
  nor nor_2 (nor_2_out, Mem_Read, Mem_Write, ANDI, ADDI);
  Multiplexer #(.width(3), .enable("false")) multiplexer_1 (
    .in0(Instruction_Input[2:0]), .in1(bit_extender_1_out), .out(Function_Code_Output), .sel(nor_1_out));
  assign bit_extender_1_out = {{2{1'b0}}, nor_2_out};  // Bit_Extender bit_extender_1
  and and_1 (JR, Instruction_Input[2], Instruction_Input[1], Rtype0001);
  and and_2 (JALR, JR, Instruction_Input[0]);
  nor nor_3 (ALU_Control, Rtype0000, ORI, ANDI);

  assign Mem_to_Reg = Mem_Read;

  // Other names for the same wires on the sheet: f0 = Instruction_Input[0];
  //   Fuction_Code[2:0] = Instruction_Input[2:0]; f1 = Instruction_Input[1]; f2 = Instruction_Input[2];
  //   Opcode[3:0] = Instruction_Input[15:12]; LW = Mem_Read; SW = Mem_Write
endmodule

module PC (
  input  [11:0] PC_Input,
  output [11:0] PC_Output
);

  wire clock_1_out;

  Clock clock_1 (.out(clock_1_out));
  Register #(.width(12)) PC (.D(PC_Input), .Q(PC_Output), .clk(clock_1_out));  // open: en, clr
endmodule

// Next_PC
module NextPC1 (
  input  [11:0] INC_PC,
  input  J,
  input  [11:0] Immediate,
  input  BLTZ,
  input  Sign,
  input  BGTZ,
  input  BEQ,
  input  BNE,
  input  Zero,
  output PCSrc,
  output [11:0] Next_Instrucrion
);

  wire and_1_out, and_2_out, and_3_out, and_4_out, not_1_out, not_2_out, not_3_out;
  wire [11:0] adder_1_out, bit_extender_1_out;

  assign bit_extender_1_out = {{6{1'b0}}, Immediate[5:0]};  // Bit_Extender bit_extender_1
  Adder #(.width(12)) adder_1 (.a(INC_PC), .b(bit_extender_1_out), .out(adder_1_out));  // open: cin, cout
  Multiplexer #(.width(12), .enable("false")) multiplexer_1 (
    .in0(adder_1_out), .in1(Immediate), .out(Next_Instrucrion), .sel(J));
  and and_1 (and_1_out, BLTZ, not_2_out, Sign);
  or or_1 (PCSrc, J, and_1_out, and_2_out, and_3_out, and_4_out);
  not not_1 (not_1_out, Sign);
  not not_2 (not_2_out, Zero);
  and and_2 (and_2_out, not_1_out, not_2_out, BGTZ);
  and and_3 (and_3_out, BEQ, Zero);
  and and_4 (and_4_out, not_3_out, BNE);
  not not_3 (not_3_out, Zero);
endmodule

module test (
  input  [2:0] rw,
  input  rwwrite_en,
  input  [15:0] busw,
  output [15:0] r1
);

  wire register_file_1_p4;

  // Register_File register_file_1: pin names not known; wires that end beside it: rw, r1, rwwrite_en, register_file_1_p4, busw
  Clock clock_1 (.out(register_file_1_p4));
endmodule
